// Logisim project pohuy.circ as structural Verilog: 2 circuits, main circuit main
module main (
  output out_1,
  output out_2
);

  wire cdm16_1_p1, cdm16_1_p2, clock, comparator_1_eq, comparator_2_eq, mem, multiplexer_3_out, not_1_out,
       read, word, wr_rd;
  wire [7:0] ext_data, pull_resistor_1_node, pull_resistor_2_node, vec_adr;
  wire [15:0] address_bus, cdm16_1_p7, cdm16_1_p8, data_bus, multiplexer_6_out;
  wire [15:8] multiplexer_2_out;

  Clock clock_1 (.out(clock));
  // Probe on cdm16_1_p1
  // cdm16 cdm16_1: pin names not known; wires that end beside it: cdm16_1_p1, cdm16_1_p2, mem, read, word, address_bus, cdm16_1_p7, cdm16_1_p8
  Multiplexer multiplexer_1 (.in0(1'b0), .in1(clock), .out(cdm16_1_p2), .sel(1'b1));  // open: en
  assign cdm16_1_p8 = read ? data_bus : 16'bz;  // Controlled_Buffer controlled_buffer_1
  Comparator #(.width(16)) comparator_1 (.a(address_bus), .b(16'hfff0), .eq(comparator_1_eq));  // open: gt, lt
  assign data_bus = not_1_out ? cdm16_1_p7 : 16'bz;  // Controlled_Buffer controlled_buffer_2
  not not_1 (not_1_out, read);
  Multiplexer #(.width(16)) multiplexer_2 (
    .in0({16{1'b0}}), .in1(data_bus), .out({multiplexer_2_out, ext_data}), .sel(comparator_1_eq));  // open: en
  Pull_Resistor pull_resistor_1 (.node(pull_resistor_1_node[0]));
  Multiplexer multiplexer_3 (
    .in0(clock), .in1(pull_resistor_1_node[0]), .out(multiplexer_3_out), .sel(pull_resistor_1_node[0]));  // open: en
  Multiplexer #(.width(8)) multiplexer_4 (
    .in0(8'he2), .in1(8'h99), .out(pull_resistor_1_node), .sel(multiplexer_3_out));  // open: en
  Comparator #(.width(16)) comparator_2 (.a(address_bus), .b(16'hfff1), .eq(comparator_2_eq));  // open: gt, lt
  Pull_Resistor pull_resistor_2 (.node(pull_resistor_2_node[0]));
  Multiplexer #(.width(8)) multiplexer_5 (
    .in0(pull_resistor_1_node), .in1(8'ha5), .out(pull_resistor_2_node), .sel(pull_resistor_2_node[0]));  // open: en
  Multiplexer #(.width(16)) multiplexer_6 (
    .in0({{15{1'b0}}, wr_rd}), .in1(data_bus), .out(multiplexer_6_out), .sel(comparator_2_eq));  // open: en
  // Probe on pull_resistor_2_node
  // RAM ram_1: pin names not known; wires that end beside it: address_bus, word, word, mem, clock, read, data_bus
  Register #(.width(1)) register_1 (.D(multiplexer_6_out[0]), .Q(wr_rd), .clk(clock));  // open: en, clr
  // UART uart_1: pin names not known; wires that end beside it: vec_adr, ext_data, out_1, clock, wr_rd, out_2, 1'b1
endmodule

module _0_0_1 (
);

  wire comparator_1_eq;
  wire [7:0] ext_data;
  wire [15:0] address_bus, data_bus;
  wire [15:8] multiplexer_1_out;

  Comparator #(.width(16)) comparator_1 (.a(address_bus), .b(16'hff), .eq(comparator_1_eq));  // open: gt, lt
  Multiplexer #(.width(16)) multiplexer_1 (
    .in0({16{1'b0}}), .in1(data_bus), .out({multiplexer_1_out, ext_data}), .sel(comparator_1_eq));  // open: en
endmodule
