// Logisim project pohuy.circ as structural Verilog: 4 circuits, main circuit main
module main (
  output out_1,
  output out_2
);

  wire \break , cdm16_1_p1, clock, comparator_1_eq, comparator_2_eq, comparator_4_eq, comparator_5_eq,
       comparator_6_eq, comparator_7_eq, comparator_8_eq, mem, multiplexer_8_out, multiplexer_9_out,
       multiplexer_10_out, not_1_out, not_2_out, read, telnet, uart_1_p5, undriven, word;
  wire [7:0] ext_data, vec_adr;
  wire [15:0] address_bus, cdm16_1_p5, cdm16_1_p6, cdm16_1_p7, command, controlled_buffer_2_out, data_bus,
       debugger_1_p1, multiplexer_4_out, multiplexer_6_out, multiplexer_7_out, multiplexer_11_out,
       multiplexer_12_out, multiplexer_13_out, multiplexer_14_out, multiplexer_17_out, num, temporary_data,
       undriven_2;
  wire [15:8] multiplexer_5_out, register_1_q;

  Clock clock_1 (.out(clock));
  // cdm16 cdm16_1: pin names not known; wires that end beside it: cdm16_1_p1, mem, read, word, cdm16_1_p5, cdm16_1_p6, cdm16_1_p7
  Multiplexer multiplexer_1 (.in0(clock), .in1(1'b0), .out(cdm16_1_p1), .sel(\break ));  // open: en
  // UART uart_1: pin names not known; wires that end beside it: vec_adr, ext_data, out_1, clock, uart_1_p5, out_2, 1'b1
  Comparator comparator_1 (.a(vec_adr), .b(8'ha), .eq(comparator_1_eq));  // open: gt, lt
  pizdec_v_kvadrate pizdec_v_kvadrate_1 (.in_3(vec_adr), .out_4(num), .in_2(clock), .in_1(comparator_2_eq));
  Comparator comparator_2 (.a(vec_adr), .b({8{1'b0}}), .eq(comparator_2_eq));  // open: gt, lt
  assign cdm16_1_p7 = read ? multiplexer_4_out : 16'bz;  // Controlled_Buffer controlled_buffer_1
  or or_1 (uart_1_p5, comparator_1_eq, \break );
  // Probe on num
  Comparator comparator_3 (.a(vec_adr), .b({8{1'b0}}), .eq(telnet));  // open: gt, lt
  Multiplexer #(.width(16)) multiplexer_2 (.in0(cdm16_1_p5), .out(address_bus), .sel(\break ));  // open: in1, en
  assign controlled_buffer_2_out = not_1_out ? cdm16_1_p6 : 16'bz;  // Controlled_Buffer controlled_buffer_2
  not not_1 (not_1_out, read);
  // Debugger debugger_1: pin names not known; wires that end beside it: debugger_1_p1
  Multiplexer #(.width(16)) multiplexer_3 (
    .in0(controlled_buffer_2_out), .in1(temporary_data), .out(data_bus), .sel(\break ));  // open: en
  Multiplexer #(.width(16)) multiplexer_4 (.in0(data_bus), .out(multiplexer_4_out), .sel(\break ));  // open: in1, en
  Comparator #(.width(16)) comparator_4 (.a(address_bus), .b(16'hffe0), .eq(comparator_4_eq));  // open: gt, lt
  Multiplexer #(.width(16)) multiplexer_5 (
    .in0({16{1'b0}}), .in1(data_bus), .out({multiplexer_5_out, ext_data}), .sel(undriven));  // open: en
  Multiplexer #(.width(16)) multiplexer_6 (
    .in0(undriven_2), .in1({16{1'b0}}), .out(multiplexer_6_out), .en(comparator_6_eq));  // open: sel
  Multiplexer #(.width(16)) multiplexer_7 (
    .in0({register_1_q, ext_data}), .in1(data_bus), .out(multiplexer_7_out), .sel(comparator_4_eq));  // open: en
  Register #(.width(16)) register_1 (
    .D(multiplexer_7_out), .Q({register_1_q, ext_data}), .clk(clock));  // open: en, clr
  Multiplexer multiplexer_8 (.in0(word), .in1(1'b0), .out(multiplexer_8_out), .sel(\break ));  // open: en
  Comparator comparator_5 (.a(vec_adr), .b(8'hd), .eq(comparator_5_eq));  // open: gt, lt
  Multiplexer multiplexer_9 (.in0(read), .in1(telnet), .out(multiplexer_9_out), .sel(\break ));  // open: en
  Multiplexer multiplexer_10 (.in0(mem), .in1(not_2_out), .out(multiplexer_10_out), .sel(\break ));  // open: en
  not not_2 (not_2_out, telnet);
  Comparator #(.width(16)) comparator_6 (.a({16{1'b0}}), .b(debugger_1_p1), .eq(comparator_6_eq));  // open: gt, lt
  Multiplexer #(.width(16)) multiplexer_11 (
    .in0(command), .in1(num), .out(multiplexer_11_out), .sel(comparator_5_eq));  // open: en
  Multiplexer #(.width(16)) multiplexer_12 (
    .in0(16'hffe2), .in1(16'hffe3), .out(multiplexer_12_out), .sel(comparator_5_eq));  // open: en
  // RAM ram_1: pin names not known; wires that end beside it: address_bus, multiplexer_8_out, multiplexer_10_out, clock, multiplexer_9_out, data_bus
  Multiplexer #(.width(16)) multiplexer_13 (
    .in0(multiplexer_11_out), .in1({16{1'b0}}), .out(multiplexer_13_out), .sel(comparator_7_eq));  // open: en
  Comparator comparator_7 (.a(vec_adr), .b(8'ha), .eq(comparator_7_eq));  // open: gt, lt
  Multiplexer #(.width(16)) multiplexer_14 (
    .in0(multiplexer_12_out), .in1(16'hffe1), .out(multiplexer_14_out), .sel(comparator_7_eq));  // open: en
  Multiplexer #(.width(16)) multiplexer_15 (.in1(multiplexer_13_out), .out(data_bus), .sel(\break ));  // open: in0, en
  Multiplexer #(.width(16)) multiplexer_16 (
    .in1(multiplexer_14_out), .out(address_bus), .sel(\break ));  // open: in0, en
  Multiplexer #(.width(16)) multiplexer_17 (
    .in0({{15{1'b0}}, \break }), .in1(data_bus), .out(multiplexer_17_out), .sel(comparator_8_eq));  // open: en
  Comparator #(.width(16)) comparator_8 (.a(address_bus), .b(16'hffe1), .eq(comparator_8_eq));  // open: gt, lt
  pizdec pizdec_1 (.intput_value(vec_adr), .output_value(command), .clock(clock));
  Register #(.width(1)) register_2 (.D(multiplexer_17_out[0]), .Q(\break ), .clk(clock));  // open: en, clr
  // Probe on command

  // Other names for the same wires on the sheet: wr_rd = \break 
endmodule

module _0_0_1 (
);

  wire comparator_1_eq;
  wire [7:0] ext_data;
  wire [15:0] address_bus, data_bus;
  wire [15:8] multiplexer_1_out;

  Comparator #(.width(16)) comparator_1 (.a(address_bus), .b(16'hff), .eq(comparator_1_eq));  // open: gt, lt
  Multiplexer #(.width(16)) multiplexer_1 (
    .in0({16{1'b0}}), .in1(data_bus), .out({multiplexer_1_out, ext_data}), .sel(comparator_1_eq));  // open: en
endmodule

module pizdec (
  input  [7:0] intput_value,
  input  clock,
  output [15:0] output_value
);

  wire comparator_1_eq, comparator_2_eq, comparator_3_eq, comparator_4_eq, comparator_5_eq, comparator_6_eq,
       not_1_out, not_2_out;
  wire [7:0] bet, call, check, fold, multiplexer_6_out, or_1_out, pull_resistor_1_node, pull_resistor_2_node,
       pull_resistor_3_node, pull_resistor_4_node, pull_resistor_5_node, raise;

  Comparator comparator_1 (.a(intput_value), .b(8'h62), .eq(comparator_1_eq));  // open: gt, lt
  Pull_Resistor pull_resistor_1 (.node(pull_resistor_1_node));
  Multiplexer #(.width(8)) multiplexer_1 (
    .in0(pull_resistor_1_node), .in1(8'h62), .out(bet), .sel(comparator_1_eq));  // open: en
  Comparator comparator_2 (.a(intput_value), .b(8'h63), .eq(comparator_2_eq));  // open: gt, lt
  Pull_Resistor pull_resistor_2 (.node(pull_resistor_2_node));
  Multiplexer #(.width(8)) multiplexer_2 (
    .in0(pull_resistor_2_node), .in1(8'h63), .out(call), .sel(comparator_2_eq));  // open: en
  Comparator comparator_3 (.a(intput_value), .b(8'h72), .eq(comparator_3_eq));  // open: gt, lt
  Pull_Resistor pull_resistor_3 (.node(pull_resistor_3_node));
  Multiplexer #(.width(8)) multiplexer_3 (
    .in0(pull_resistor_3_node), .in1(8'h72), .out(raise), .sel(comparator_3_eq));  // open: en
  Comparator comparator_4 (.a(intput_value), .b(8'h6b), .eq(comparator_4_eq));  // open: gt, lt
  Pull_Resistor pull_resistor_4 (.node(pull_resistor_4_node));
  Multiplexer #(.width(8)) multiplexer_4 (
    .in0(pull_resistor_4_node), .in1(8'h6b), .out(check), .sel(comparator_4_eq));  // open: en
  Pull_Resistor pull_resistor_5 (.node(pull_resistor_5_node));
  Comparator comparator_5 (.a(intput_value), .b(8'h66), .eq(comparator_5_eq));  // open: gt, lt
  Multiplexer #(.width(8)) multiplexer_5 (
    .in0(pull_resistor_5_node), .in1(8'h66), .out(fold), .sel(comparator_5_eq));  // open: en
  assign or_1_out = bet | call | raise | check | fold;  // OR_Gate or_1, 8 bits wide
  Register register_1 (.D(multiplexer_6_out), .Q(output_value[7:0]), .clk(not_1_out));  // open: en, clr
  Multiplexer #(.width(8)) multiplexer_6 (
    .in0(output_value[7:0]), .in1(or_1_out), .out(multiplexer_6_out), .sel(not_2_out));  // open: en
  not not_1 (not_1_out, clock);
  not not_2 (not_2_out, comparator_6_eq);
  Comparator comparator_6 (.a(or_1_out), .b({8{1'b0}}), .eq(comparator_6_eq));  // open: gt, lt

  assign output_value[15:8] = {8{1'b0}};

  // Other names for the same wires on the sheet: input_value[7:0] = intput_value
endmodule

module pizdec_v_kvadrate (
  input  in_1,
  input  in_2,
  input  [7:0] in_3,
  output [15:0] out_4
);

  wire and_1_out, comparator_1_gt, comparator_2_lt, not_1_out;
  wire [7:0] adder_1_out, multiplexer_1_out, multiplexer_2_out, multiplier_1_out, subtractor_1_out;

  Comparator comparator_1 (.a(in_3), .b(8'h29), .gt(comparator_1_gt));  // open: eq, lt
  Comparator comparator_2 (.a(in_3), .b(8'h40), .lt(comparator_2_lt));  // open: gt, eq
  and and_1 (and_1_out, comparator_1_gt, comparator_2_lt);
  Multiplexer #(.width(8)) multiplexer_1 (
    .in0({8{1'b0}}), .in1(subtractor_1_out), .out(multiplexer_1_out), .sel(and_1_out));  // open: en
  Subtractor subtractor_1 (.a(in_3), .b(8'h30), .out(subtractor_1_out));  // open: bin, bout
  Adder adder_1 (.a(multiplexer_2_out), .b(multiplexer_1_out), .out(adder_1_out));  // open: cin, cout
  not not_1 (not_1_out, in_2);
  Register register_1 (.D(adder_1_out), .Q(out_4[7:0]), .clk(not_1_out), .clr(in_1));  // open: en
  Multiplexer #(.width(8)) multiplexer_2 (
    .in0(out_4[7:0]), .in1(multiplier_1_out), .out(multiplexer_2_out), .sel(and_1_out));  // open: en
  Multiplier multiplier_1 (.a(out_4[7:0]), .b(8'ha), .out(multiplier_1_out));  // open: cin, cout

  assign out_4[15:8] = {8{1'b0}};

  // Other names for the same wires on the sheet: input_num[7:0] = in_3; output_num[7:0] = out_4[7:0]
endmodule
